# Fritzing sketch raspberry_pi0 (saved by Fritzing 0.9.3b)
breadboards: 1

parts:
  RHT1 = Humidity and Temperature Sensor RHT03
  R1 = Resistor [tolerance=±5% resistance=10k package=THT]
  Raspberry_Pi_Zero1 = Raspberry Pi Zero

nets:
  3V3: RHT1.Vcc, R1.Pin_1, Raspberry_Pi_Zero1.3v3, Raspberry_Pi_Zero1.3V3
  N1: RHT1.Data-signal, R1.Pin_0, Raspberry_Pi_Zero1.GPIO2
